# Fritzing sketch DrumIlluminator (saved by Fritzing 0.9.2b)
breadboards: 2

parts:
  IC1 = ULN2803A [package=THT]
  Parte1 = Arduino Uno (Rev3)
  S1 = Pushbutton [package="[THT]"]
  S2 = Pushbutton [package="[THT]"]
  R22 = Resistor [tolerance=±5% resistance=220 package="0805 [SMD]"]
  R23 = Resistor [tolerance=±5% resistance=220 package="0805 [SMD]"]
  R24 = Resistor [tolerance=±5% resistance=220 package="0805 [SMD]"]
  LED6 = Super Flux RGB LED (com. anode)
  Alimentación_5v = 4 x AAA Battery Mount
  S3 = Pushbutton [package="[THT]"]
  S4 = Pushbutton [package="[THT]"]
  R25 = 1 MΩ Resistor [package=THT]
  J1 = Piezo Speaker
  J2 = Piezo Speaker
  J3 = Piezo Speaker
  J4 = Piezo Speaker
  LED7 = Super Flux RGB LED (com. anode)
  R28 = Resistor [tolerance=±5% resistance=220 package="0805 [SMD]"]
  R29 = Resistor [tolerance=±5% resistance=220 package="0805 [SMD]"]
  R30 = Resistor [tolerance=±5% resistance=220 package="0805 [SMD]"]
  LED8 = Super Flux RGB LED (com. anode)
  R31 = Resistor [tolerance=±5% resistance=220 package="0805 [SMD]"]
  R32 = Resistor [tolerance=±5% resistance=220 package="0805 [SMD]"]
  R33 = Resistor [tolerance=±5% resistance=220 package="0805 [SMD]"]
  LED9 = Super Flux RGB LED (com. anode)
  R34 = Resistor [tolerance=±5% resistance=220 package="0805 [SMD]"]
  R35 = Resistor [tolerance=±5% resistance=220 package="0805 [SMD]"]
  R36 = Resistor [tolerance=±5% resistance=220 package="0805 [SMD]"]
  R37 = Resistor [tolerance=±5% resistance=220 package=THT]
  Resistencia_10KOhm1 = Resistor 10K [package="2010 [SMD]"]
  R27 = 1 MΩ Resistor [package=THT]
  R26 = 1 MΩ Resistor [package=THT]
  Resistencias_1_MΩ_-_Piezoeléctricos = 1 MΩ Resistor [package=THT]
  Resistencia_10KOhm2 = Resistor 10K [package="2010 [SMD]"]
  Resistencia_10KOhm3 = Resistor 10K [package="2010 [SMD]"]
  Resistencia_10KOhm4 = Resistor 10K [package="2010 [SMD]"]
  R38 = Resistor [tolerance=±5% resistance=220 package=THT]
  R39 = Resistor [tolerance=±5% resistance=220 package=THT]
  R40 = Resistor [tolerance=±5% resistance=220 package=THT]
  Tiras_de_LED_RGB = Super Flux RGB LED (com. anode)
  LED11 = Super Flux RGB LED (com. anode)
  R41 = Resistor [tolerance=±5% resistance=220 package="0805 [SMD]"]
  R42 = Resistor [tolerance=±5% resistance=220 package="0805 [SMD]"]
  R43 = Resistor [tolerance=±5% resistance=220 package="0805 [SMD]"]
  R44 = Resistor [tolerance=±5% resistance=220 package="0805 [SMD]"]
  R45 = Resistor [tolerance=±5% resistance=220 package="0805 [SMD]"]
  R46 = Resistor [tolerance=±5% resistance=220 package="0805 [SMD]"]
  R47 = 1 MΩ Resistor [package=THT]
  R48 = 1 MΩ Resistor [package=THT]
  PIEZOELÉCTRICOS = Piezo Speaker
  J6 = Piezo Speaker

nets:
  N1: IC1.In_3, R22.Pin_0, R29.Pin_0, R32.Pin_0, R35.Pin_0, R43.Pin_0, R44.Pin_0
  N2: IC1.In_4, R41.Pin_0, R45.Pin_0
  N3: IC1.In_5, R42.Pin_0, R46.Pin_0
  N4: IC1.In_6, R23.Pin_0, R24.Pin_0
  N5: IC1.In_7, R28.Pin_0, R30.Pin_0
  N6: IC1.In_8, R31.Pin_0, R33.Pin_0
  N7: IC1.0V, R34.Pin_0, R36.Pin_0
  N8: IC1.COM_-_Common, Parte1.D2
  N9: IC1.Out_8, Parte1.D3_PWM
  N10: IC1.Out_7, Parte1.D4
  N11: IC1.Out_6, Parte1.D5_PWM
  N12: IC1.Out_5, Parte1.D6_PWM
  N13: IC1.Out_4, Parte1.D7
  N14: IC1.Out_3, Parte1.D8
  N15: Parte1.A0, J1.pin2, Resistencias_1_MΩ_-_Piezoeléctricos.Pin_0
  N16: Parte1.A1, J2.pin2, R27.Pin_0
  N17: Parte1.A2, J3.pin2, R26.Pin_0
  N18: Parte1.A3, R25.Pin_0, J4.pin2
  N19: Parte1.A4/SDA, R47.Pin_0, J6.pin2
  N20: Parte1.A5/SCL, R48.Pin_0, PIEZOELÉCTRICOS.pin2
  N21: Parte1.D9_PWM, S1.Pin_3, S1.Pin_4, Resistencia_10KOhm1.Pin_1
  N22: Parte1.D10_PWM/SS, S2.Pin_3, S2.Pin_4, Resistencia_10KOhm2.Pin_1
  N23: Parte1.D11_PWM/MOSI, S3.Pin_3, S3.Pin_4, Resistencia_10KOhm3.Pin_1
  N24: Parte1.D12/MISO, S4.Pin_3, S4.Pin_4, Resistencia_10KOhm4.Pin_1
  N25: S1.Pin_1, S1.Pin_2, R37.Pin_0
  N26: S2.Pin_1, S2.Pin_2, R38.Pin_0
  N27: R22.Pin_1, LED6.common_anode
  N28: R23.Pin_1, LED6.blue_cathode
  N29: R24.Pin_1, LED6.green_cathode
  N30: LED6.red_cathode, Alimentación_5v.+, LED7.red_cathode, LED8.red_cathode, LED9.red_cathode, R37.Pin_1, R38.Pin_1, R39.Pin_1, R40.Pin_1, Tiras_de_LED_RGB.red_cathode, LED11.red_cathode
  N31: Alimentación_5v.-, R25.Pin_1, J1.pin1, J2.pin1, J3.pin1, J4.pin1, Resistencia_10KOhm1.Pin_0, R27.Pin_1, R26.Pin_1, Resistencias_1_MΩ_-_Piezoeléctricos.Pin_1, Resistencia_10KOhm2.Pin_0, Resistencia_10KOhm3.Pin_0, Resistencia_10KOhm4.Pin_0, R47.Pin_1, R48.Pin_1, PIEZOELÉCTRICOS.pin1, J6.pin1
  N32: S3.Pin_1, S3.Pin_2, R39.Pin_0
  N33: S4.Pin_1, S4.Pin_2, R40.Pin_0
  N34: LED7.blue_cathode, R30.Pin_1
  N35: LED7.green_cathode, R28.Pin_1
  N36: LED7.common_anode, R29.Pin_1
  N37: LED8.blue_cathode, R33.Pin_1
  N38: LED8.green_cathode, R31.Pin_1
  N39: LED8.common_anode, R32.Pin_1
  N40: LED9.blue_cathode, R36.Pin_1
  N41: LED9.green_cathode, R34.Pin_1
  N42: LED9.common_anode, R35.Pin_1
  N43: Tiras_de_LED_RGB.blue_cathode, R45.Pin_1
  N44: Tiras_de_LED_RGB.green_cathode, R41.Pin_1
  N45: Tiras_de_LED_RGB.common_anode, R43.Pin_1
  N46: LED11.blue_cathode, R46.Pin_1
  N47: LED11.green_cathode, R42.Pin_1
  N48: LED11.common_anode, R44.Pin_1

notes:
  Esta placa de pruebas no está en el montaje real pero se ha añadido en esteesquema para aportar claridad.

custom parts:
  1 MΩ Resistor: A generic 5-band resistor (0.25W)
  Resistor 10K: Resistor Basic schematic elements and footprints for 0603, 1206, and PTH resistors.

// code stored in the sketch: DrumIlluminator.ino
/****************************************************
*  Programa "DrumIlluminator.ino" para Arduino UNO
*
* Archivo:  DrumIlluminator.ino
* Autor:    Jorge Ignacio Balanz Pino
* Fecha:    mayo de 2016
* Descripción: Programa principal para Arduino UNO.
*     Hace que se ilumine una batería acústica,
*     conectando unos sensores piezoeléctricos a
*     cada tambor (o componente) de la batería e
*     introduciendo en su interior unos LED.
*
****************************************************/

//Incluyo una librería de creación propia,
//  desde la que se hacen el resto 
//  de importaciones necesarias:
#include "DumIlluminatorFunctions.h"

//Cabeceras de funciones (definidas en este archivo):
void showLogo(boolean withserial=false);
void updateThresholds(boolean up);
void checkTimers();
void checkButtons();

//Constantes
const int thresUpPin = 9;  // Pin Arduino para subir los umbrales.
const int thresDwnPin = 10; // Pin Arduino para bajar los umbrales.
const int testPin = 11;  // Pin Arduino para lanzar un test de los LED.
const int lightPinIn = 12; // Pin Arduino para poner o quitar la iluminación constante (ENTRADA).
const int lightPinOut = 8; // Pin Arduino para poner o quitar la iluminación constante (SALIDA).
const int signaling = 13; //Pin Arduino que se utilizará para algunas señalizaciones.
const boolean T_UP = true;  // alias de true para simbolizar subida de umbral
const boolean T_DOWN = false;  // alias de false para simbolizar bajada de umbral
const int THRES_INTERVAL = 50; // Unidades en que se aumentan o disminuyen los umbrales
const long REPOSO = 5000; //Tiempo de inactividad que se considera para reposo.
const int LIGHT_DELAY = 100; //Tiempo que los LED se quedan encendidos cuando un sensor detecta algo.
const boolean __DEBUG = true; //Indica si se debe escribir información de debug por el puerto serie
const boolean __WITH_LCD = false; //Indica si hay un LCD conectado al puerto I2C (SDA-SCL o A4-A5)
const boolean __ACTIV_LCD = true; //Indica si se debe escribir información de entradas analógicas en el LCD (sólo si __WITH_LCD=true)

//Variables globales:
LiquidCrystal_I2C lcd(0x27,16,2);  // Establece la dirección 0x27 para el LCD de 16 caracteres y dos líneas. La variable "lcd" es el Objeto LCD 

byte ledarray[] = {2,3,4,5,6,7}; //Salidas para los LED que se deben encender.
int thresholds[] = {500, 500, 500, 500, 500, 500}; //Array de 6 enteros que representan los umbrales que indican si se enciende un LED.
int analogics[] = {A0,A1,A2,A3,A4,A5}; //Array de entradas analógicas a escanear.
long lightstime[] = {0,0,0,0,0,0}; //Array de temporizadores para dejar los LED: recoge los instantes en que debe apagarse cada LED.
int lastAnalogIndex = 5; //Índice en el que se terminan de escanear entradas analógicas.
long ultimaactividad = 0; //Tiempo (timestamp) para controlar el tiempo de inactividad y presentar logo en el LCD (si está conectado).

/*** INICIALIZACIÓN ***/
void setup()
{
  /*
   * MISCELÁNEA
   */
   //Inicializar Serial:
  if(__DEBUG){
     Serial.begin (9600); //Inicializamos comunicación serie
  }

  /*
   * DISPLAY (LCD 16x2)
   */
  if(__WITH_LCD){
    //Si se ha utiliza el LCD, sólo se usan 4 entradas analógicas como máximo
    lastAnalogIndex = (lastAnalogIndex>3 ? 3 : lastAnalogIndex); //A4 y A5 se usan para el LCD (I2C 0x27 / SCL-SDA)
    initializeLCD(lcd); //Inicio y Presentación en el LCD
  }
  //Mostramos presentación
  showLogo(true);
  delay(500);

  //Establecemos el modo de los pines
  for(int i=0; i<=lastAnalogIndex; i++){
    pinMode(ledarray[i], OUTPUT);
  }
  //Pin de señalización
  pinMode(signaling,OUTPUT); //Este pin señalizará ciertas actividades

  //Pines para funciones añadidas
  pinMode(thresUpPin, INPUT);
  pinMode(thresDwnPin, INPUT);
  pinMode(testPin, INPUT);
  pinMode(lightPinIn, INPUT);
  pinMode(lightPinOut, OUTPUT);//Salida!!

  //Hacemos una comprobación de LED al inicio:
  checkLEDS(1000);
  
} //Fin SETUP

/*** ITERACIÓN ***/
void loop()
{
  
  //Comprobamos los diferentes temporizadores:
  checkTimers();

  //Comprobamos los botones:
  checkButtons();
 
  //REALIZAMOS LECTURA DE LAS ENTRADAS ANALÓGICAS
  checkAnalogics();
  
} //Fin LOOP


/********************************************
 *          FUNCIONES AUXILIARES            *
 ********************************************/

////////   PROCESAR I/O   ///////////////////
/**
 * Hacer una lectura de las entradas analógicas y 
 * establecer en HIGH las salidas apropiadas:
 */
void checkAnalogics(){
  int lectura = 0;
  //Se comprueba cada entrada analógica:
  for(int i=0; i<=lastAnalogIndex; i++){
    //Sólo se comprueba la entrada si el temporizador ha caducado (es 0)
    if(lightstime[i]==0){
      lectura = analogRead(analogics[i]); //Leemos entrada analógica.
      //Comprobamos si supera su umbral
      if(lectura>thresholds[i]){
        //Si supera el umbral:
        digitalWrite(ledarray[i], HIGH); //Encendemos su LED
        lightstime[i] = millis()+LIGHT_DELAY; //Ponemos su temporizador
        //Presentamos el evento
        if(__DEBUG){
          Serial.println("Umbral superado en 'A"+ String(i) +"': "+String(lectura));
        }
        //Presentarlo en el LCD
        if(__WITH_LCD){
          ultimaactividad = millis()+REPOSO;
          if(__ACTIV_LCD){ //Sólo si hay que indicar la actividad por el LCD      
            lcd.clear();
            LCDwriteText(lcd,"Lectura de 'A"+ String(i) +"':",0,0);
            LCDwriteNumber(lcd,lectura,1,4);
          }
        }
      }
      else{
        //Si había que comprobar la entrada y no se supera el umbral, se apaga:
        digitalWrite(ledarray[i], LOW); //Apagamos su LED
      }
    }
  }
}

/**
 * Comprobar si se ha pulsado alguno de los botones
 */
void checkButtons(){
  int aux = digitalRead(thresUpPin);
  
  //Controlamos si se solicita cambio de umbrales
  if(aux == HIGH){
    updateThresholds(T_UP); //BOTÓN SUBIR
    delay(500); //Pulsación de 1/2 segundo máximo
  }
  aux = digitalRead(thresDwnPin); //BOTÓN BAJAR
  if(aux == HIGH){
    updateThresholds(T_DOWN);
    delay(500);
  }
  //Controlamos si se solicita Test de LED
  aux = digitalRead(testPin); //BOTÓN TEST
  if(aux == HIGH){
    checkLEDS(500);
  }
  //Controlamos si se solicita iluminación constante
  aux = digitalRead(lightPinIn); //BOTÓN Iluminación
  if(aux == HIGH){
    aux=digitalRead(lightPinOut);
    if(aux==HIGH){
      digitalWrite(lightPinOut,LOW);
      if(__WITH_LCD){
        ultimaactividad = millis()+REPOSO;
        lcd.clear();
        LCDwriteText(lcd,"¡Apagar Luces!",0,1);
      }
      if(__DEBUG){
        Serial.println("----------------------------------");
        Serial.println("    >>>>  Apagar Luces!! <<<<");  
        Serial.println("----------------------------------");
      }
    }
    else{
      digitalWrite(lightPinOut,HIGH);
      if(__WITH_LCD){
        ultimaactividad = millis()+REPOSO;
        lcd.clear();
        LCDwriteText(lcd,"¡Encender Luces!",0,0);
      }
      if(__DEBUG){
        Serial.println("----------------------------------");
        Serial.println("    >>>>  Encender Luces!! <<<<");  
        Serial.println("----------------------------------");
      }
    }

    delay(500);
  }  
}

///////////  MODIFICAR UMBRALES   ///////////////////
/**
 * Subir o bajar los umbrales a superar.
 * El porcentaje de incremento se establece en la constante THRES_INTERVAL.
 */
void updateThresholds(boolean up){
  if(up){
    for(int i=0; i<6; i++){
      thresholds[i] += THRES_INTERVAL;
      if(thresholds[i]>1000) //Limitamos el rango
        thresholds[i]=1000;
    }
  }
  else{
    for(int i=0; i<6; i++){
      thresholds[i] -= THRES_INTERVAL;
      if(thresholds[i]<THRES_INTERVAL)
        thresholds[i]=THRES_INTERVAL;
    }
  }
  //Presentamos los cambios, si procede:
  if(__WITH_LCD){
    String s = "A"+String(thresholds[0])+"; C"+String(thresholds[2])+"; E"+String(thresholds[4]);
    lcd.clear();
    LCDwriteText(lcd,"Cambio Umbrales:",0,0);
    LCDwriteText(lcd,s,1,0);
    ultimaactividad = millis()+REPOSO;
  }
  if(__DEBUG){
    Serial.println("----------------------------------");
    Serial.print(">>>> Cambio de Umbrales ");
    if(up) 
      Serial.println("(UP):");
    else
      Serial.println("(DWN):");  
    for(int i=0; i<6; i++){
      Serial.println("\t@ A"+String(i)+" --> "+String(thresholds[i]));
    }
    Serial.println("----------------------------------");
  }
}

/********************************
*			DISPLAY
*********************************/
/////////    MENSAJES DISPLAY   /////////////////////
/**
 * Presentar en el display un texto de espera/reposo:
 */
void showLogo(boolean withserial){
  if(__WITH_LCD){
    lcd.backlight();
    lcd.clear();
    LCDwriteText(lcd,"Drum-Illuminator",0,0);
    LCDwriteText(lcd,"By Jorge Balanz!",1,0);
  }
  if(withserial && __DEBUG){
    Serial.println("***********************************************");
    Serial.println("      Bienvenido al DrumIlluminator!");
    Serial.println("         (By Jorge Balanz)");
    if(!__WITH_LCD)
      Serial.println("      Funcionamiento SIN Display LCD.");
    Serial.println("***********************************************\n");
  }
}

/***********
*    OTROS
************/
/**
 * Comprobar los temporizadores
 */
void checkTimers(){
  long t = 0;

  t = millis(); //Momento actual
   
  //Controlamos si se ha superado tiempo inactividad
  //Esto sólo se utiliza para presentar el "logo" en el
  // display LCD
  if(__WITH_LCD && (ultimaactividad>0) && (t > ultimaactividad)){
    showLogo(); //Texto de estado "en reposo"
    ultimaactividad = 0; //Reseteo para refrescar sólo una vez
    //Lo selñalizo en el pin 13
    digitalWrite(signaling, HIGH);
    delay(LIGHT_DELAY); //Señalizo el tiempo que dura encendido un tambor
    digitalWrite(signaling, LOW);
  }

  //Comprobamos los temporizadores de los LED que estén encendidos:
  for (int k=0; k<=lastAnalogIndex; k++){
    if(t>lightstime[k]){
      lightstime[k] = 0; // Ponemos el temporizador de esa luz a 0
    }
  }
  
}
/**
 * Hacer un chequeo de los colores de los LEDs
 * El chequeo debe encender las luces en el siguiente orden: 
 *  Verde, Azul, Rojo,
 *  VerdeAzul, RojoAzul, VerdeRojo,
 *  VerdeAzulRojo.
 * 
 * @param arr Array de Bytes que se utilizará para cargar los datos en los registros de desplazamiento
 * @param dely Tiempo de espera con cada color de prueba.
 * @param lcd Display LCD (objeto) donde se imprimirá información del test.
 */
void checkLEDS(int dely){
  if(__WITH_LCD){
    lcd.clear();
    LCDwriteText(lcd,"Comienza el Test:",0,0);
    delay(1500);
  }
  if(__DEBUG){
    Serial.println("**********************************************************");
    Serial.println("   Comienza el Test de LED...");
    Serial.println("\n\tENCENDER: ");
  }
  for(int i=0; i<=lastAnalogIndex; i++){
    digitalWrite(ledarray[i],HIGH);
    if(__WITH_LCD){
      lcd.clear();
      LCDwriteText(lcd,"ENCIENDE LED "+String(i),0,1);
    }
    if(__DEBUG){
      Serial.print("\tLED "+String(i));
    }
    delay(dely);
  }
  if(__DEBUG){
    Serial.println("\n\tAPAGAR: ");
  }
  for(int i=0; i<=lastAnalogIndex; i++){
    digitalWrite(ledarray[i],LOW);
    if(__WITH_LCD){
      lcd.clear();
      LCDwriteText(lcd,"APAGA LED "+String(i),0,2);
    }
    if(__DEBUG){
      Serial.print("\tLED "+String(i));
    }
    delay(dely);    
  }
  if(__WITH_LCD){
    lcd.clear();
    LCDwriteText(lcd,"TODOS!",0,3);
  }
  if(__DEBUG){
    Serial.print("\n\tTODOS JUNTOS!");
  }
  for(int i=0; i<=lastAnalogIndex; i++){
    digitalWrite(ledarray[i],HIGH);
  }
  delay(dely);    
  for(int i=0; i<=lastAnalogIndex; i++){
    digitalWrite(ledarray[i],LOW);
  }
  if(__WITH_LCD){
    showLogo();
  }
  if(__DEBUG){
    Serial.println("\n\t\tTest Finalizado!");
    Serial.println("**********************************************************\n");
  }
}
