# Fritzing sketch DrumIlluminator_With_LCD (saved by Fritzing 0.9.2b)
breadboards: 2

parts:
  IC1 = ULN2803A [package=THT]
  Parte1 = Arduino Uno (Rev3)
  S1 = Pushbutton [package="[THT]"]
  S2 = Pushbutton [package="[THT]"]
  R22 = Resistor [tolerance=±5% resistance=220 package="0805 [SMD]"]
  R23 = Resistor [tolerance=±5% resistance=220 package="0805 [SMD]"]
  R24 = Resistor [tolerance=±5% resistance=220 package="0805 [SMD]"]
  Tiras_de_LED_RGB = Super Flux RGB LED (com. anode)
  Display_LCD_16x2_con_interfaz_I2C = DeuLigne 1.1 - The Snootlab's LCD shield for Arduino
  Alimentación_a_5v = 4 x AAA Battery Mount
  S3 = Pushbutton [package="[THT]"]
  S4 = Pushbutton [package="[THT]"]
  R25 = 1 MΩ Resistor [package=THT]
  PIEZOELÉCTRICOS = Piezo Speaker
  J2 = Piezo Speaker
  J3 = Piezo Speaker
  J4 = Piezo Speaker
  LED7 = Super Flux RGB LED (com. anode)
  R28 = Resistor [tolerance=±5% resistance=220 package="0805 [SMD]"]
  R29 = Resistor [tolerance=±5% resistance=220 package="0805 [SMD]"]
  R30 = Resistor [tolerance=±5% resistance=220 package="0805 [SMD]"]
  LED8 = Super Flux RGB LED (com. anode)
  R31 = Resistor [tolerance=±5% resistance=220 package="0805 [SMD]"]
  R32 = Resistor [tolerance=±5% resistance=220 package="0805 [SMD]"]
  R33 = Resistor [tolerance=±5% resistance=220 package="0805 [SMD]"]
  LED9 = Super Flux RGB LED (com. anode)
  R34 = Resistor [tolerance=±5% resistance=220 package="0805 [SMD]"]
  R35 = Resistor [tolerance=±5% resistance=220 package="0805 [SMD]"]
  R36 = Resistor [tolerance=±5% resistance=220 package="0805 [SMD]"]
  R37 = Resistor [tolerance=±5% resistance=220 package=THT]
  Resistencia_10KOhm1 = Resistor 10K [package="2010 [SMD]"]
  R27 = 1 MΩ Resistor [package=THT]
  R26 = 1 MΩ Resistor [package=THT]
  Resistencias_1_MΩ_-_Piezoeléctricos = 1 MΩ Resistor [package=THT]
  Resistencia_10KOhm2 = Resistor 10K [package="2010 [SMD]"]
  Resistencia_10KOhm3 = Resistor 10K [package="2010 [SMD]"]
  Resistencia_10KOhm4 = Resistor 10K [package="2010 [SMD]"]
  R38 = Resistor [tolerance=±5% resistance=220 package=THT]
  R39 = Resistor [tolerance=±5% resistance=220 package=THT]
  R40 = Resistor [tolerance=±5% resistance=220 package=THT]

nets:
  N1: IC1.In_3, R22.Pin_0, R29.Pin_0, R32.Pin_0, R35.Pin_0
  N2: IC1.In_6, R23.Pin_0, R24.Pin_0
  N3: IC1.In_7, R28.Pin_0, R30.Pin_0
  N4: IC1.In_8, R31.Pin_0, R33.Pin_0
  N5: IC1.0V, R34.Pin_0, R36.Pin_0
  N6: IC1.COM_-_Common, Parte1.D2
  N7: IC1.Out_8, Parte1.D3_PWM
  N8: IC1.Out_7, Parte1.D4
  N9: IC1.Out_6, Parte1.D5_PWM
  N10: IC1.Out_3, Parte1.D8
  N11: Parte1.A0, PIEZOELÉCTRICOS.pin2, Resistencias_1_MΩ_-_Piezoeléctricos.Pin_0
  N12: Parte1.A1, J2.pin2, R27.Pin_0
  N13: Parte1.A2, J3.pin2, R26.Pin_0
  N14: Parte1.A3, R25.Pin_0, J4.pin2
  N15: Parte1.A4/SDA, Display_LCD_16x2_con_interfaz_I2C.A4(SDA)
  N16: Parte1.A5/SCL, Display_LCD_16x2_con_interfaz_I2C.A5(CLK)
  N17: Parte1.D9_PWM, S1.Pin_3, S1.Pin_4, Resistencia_10KOhm1.Pin_1
  N18: Parte1.D10_PWM/SS, S2.Pin_3, S2.Pin_4, Resistencia_10KOhm2.Pin_1
  N19: Parte1.D11_PWM/MOSI, S3.Pin_3, S3.Pin_4, Resistencia_10KOhm3.Pin_1
  N20: Parte1.D12/MISO, S4.Pin_3, S4.Pin_4, Resistencia_10KOhm4.Pin_1
  5V: Parte1.5V, Display_LCD_16x2_con_interfaz_I2C.+5V
  GND: Parte1.GND, Display_LCD_16x2_con_interfaz_I2C.GND
  N21: S1.Pin_1, S1.Pin_2, R37.Pin_0
  N22: S2.Pin_1, S2.Pin_2, R38.Pin_0
  N23: R22.Pin_1, Tiras_de_LED_RGB.common_anode
  N24: R23.Pin_1, Tiras_de_LED_RGB.blue_cathode
  N25: R24.Pin_1, Tiras_de_LED_RGB.green_cathode
  N26: Tiras_de_LED_RGB.red_cathode, Alimentación_a_5v.+, LED7.red_cathode, LED8.red_cathode, LED9.red_cathode, R37.Pin_1, R38.Pin_1, R39.Pin_1, R40.Pin_1
  N27: Alimentación_a_5v.-, R25.Pin_1, PIEZOELÉCTRICOS.pin1, J2.pin1, J3.pin1, J4.pin1, Resistencia_10KOhm1.Pin_0, R27.Pin_1, R26.Pin_1, Resistencias_1_MΩ_-_Piezoeléctricos.Pin_1, Resistencia_10KOhm2.Pin_0, Resistencia_10KOhm3.Pin_0, Resistencia_10KOhm4.Pin_0
  N28: S3.Pin_1, S3.Pin_2, R39.Pin_0
  N29: S4.Pin_1, S4.Pin_2, R40.Pin_0
  N30: LED7.blue_cathode, R30.Pin_1
  N31: LED7.green_cathode, R28.Pin_1
  N32: LED7.common_anode, R29.Pin_1
  N33: LED8.blue_cathode, R33.Pin_1
  N34: LED8.green_cathode, R31.Pin_1
  N35: LED8.common_anode, R32.Pin_1
  N36: LED9.blue_cathode, R36.Pin_1
  N37: LED9.green_cathode, R34.Pin_1
  N38: LED9.common_anode, R35.Pin_1

notes:
  El cableado no corresponde con la realidad. El pin SDA del interfaz I2C va a la entrada analógica A4 del Arduino y el pin SCL a la entrada analógica A5.
  Esta placa de pruebas no está en el montaje real pero se ha añadido en esteesquema para aportar claridad.

custom parts:
  1 MΩ Resistor: A generic 5-band resistor (0.25W)
  Resistor 10K: Resistor Basic schematic elements and footprints for 0603, 1206, and PTH resistors.

// code stored in the sketch: DrumIlluminator.ino

